# Fritzing sketch bio-blink-fade (saved by Fritzing 1.0.2b)
breadboards: 1

parts:
  Part1 = Adafruit ESP32-S3 TFT Feather [part_number="Adafruit #5483"]
  R1 = Resistor [tolerance=±5% power=0.25W resistance=100 package=THT]
  LED1 = LED - 5mm [color="Red (633nm)" current=0.030A package="5 mm [THT]"]

nets:
  N1: Part1.GND, LED1.cathode
  N2: Part1.D5, R1.Pin_0
  N3: R1.Pin_1, LED1.anode

custom parts:
  Adafruit ESP32-S3 TFT Feather: We've got a new machine here at Adafruit, it can uncover your deepest desires. Don't believe me? I'll turn it on right now to prove it to you! What, you want your very own soft serve ice cream machine? OK well, that's not something we can provide. But we can provide your second-deepest desire: an ESP32-S3 Feather board with a built in IPS TFT color display. It's got all the delicious creamy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
